# Fritzing sketch smart-radar (saved by Fritzing 0.9.3b)
breadboards: 1

parts:
  Componente1 = Arduino Uno (Rev3) - ICSP
  hc-sr1 = hc-sr04
  S1 = Pushbutton [package="[SMD]"]
  J2 = Basic Servo
  LED1 = smd LED [color="Red (633nm)" package="0805 [SMD]"]
  LED2 = smd LED [color="Red (633nm)" package="0805 [SMD]"]
  R2 = Resistor [tolerance=±5% resistance=220 package="0603 [SMD]"]
  R3 = Resistor [tolerance=±5% resistance=220 package="0603 [SMD]"]
  R4 = Resistor [tolerance=±5% resistance=10k package=THT]
  S2 = Pushbutton [package="[SMD]"]
  R5 = Resistor [tolerance=±5% resistance=10k package=THT]
  R6 = Resistor [tolerance=±5% resistance=10k package=THT]
  S3 = Pushbutton [package="[SMD]"]
  R7 = Rotary Potentiometer (Small) [maximum_resistance=100kΩ package=THT]
  part = HC-SR501 Body Sensor Module

nets:
  N1: Componente1.A0, R7.wiper
  VCC: Componente1.5V, hc-sr1.VCC, S1.Pin_3, S1.Pin_4, S2.Pin_3, S2.Pin_4, S3.Pin_3, S3.Pin_4, R7.leg2, part.VCC
  N2: Componente1.D9_PWM, LED2.anode
  N3: Componente1.D10_PWM/SS, J2.pulse
  N4: Componente1.D11_PWM/MOSI, hc-sr1.Echo
  N5: Componente1.D12/MISO, hc-sr1.Trig
  N6: Componente1.D13/SCK, LED1.anode
  N7: Componente1.D2, part.OUT
  N8: Componente1.D3_PWM, S1.Pin_1, S1.Pin_2, R4.Pin_0
  N9: Componente1.D4, S2.Pin_1, S2.Pin_2, R5.Pin_0
  N10: Componente1.D5_PWM, R6.Pin_0, S3.Pin_1, S3.Pin_2
  GND: Componente1.GND, hc-sr1.GND, R2.Pin_0, R3.Pin_0, R4.Pin_1, R5.Pin_1, R6.Pin_1, R7.leg1, part.GND
  N11: LED1.cathode, R3.Pin_1
  N12: LED2.cathode, R2.Pin_1

custom parts:
  HC-SR501 Body Sensor Module: Pyroelectric Infrared PIR Motion Sensor Detector Module
